// Logisim project Jade P_Lab 10 My First Calculator.circ as structural Verilog: 3 circuits, main circuit Full Adder
module Full_Adder (
  input  A,
  input  B,
  input  C0,
  output SUM,
  output CARRY
);

  wire and_1_out, and_2_out, xor_1_out;

  xor xor_1 (xor_1_out, A, B);
  and and_1 (and_1_out, A, B);
  xor xor_2 (SUM, xor_1_out, C0);
  and and_2 (and_2_out, xor_1_out, C0);
  or or_1 (CARRY, and_2_out, and_1_out);
endmodule

module Binary_to_7_seg_with_2_displays (
  input  S0,
  input  S1,
  input  S2,
  input  S3,
  output aL_dL_eL_fL,
  output aR,
  output bR,
  output cR,
  output dR,
  output eR,
  output fR,
  output gR
);

  wire not_1_out, not_2_out, not_3_out, not_4_out, S0_prime_S1_prime_S2_out, S0_prime_S1S2_prime_out,
       S0_prime_S1S3_prime_out, S0_prime_S2_out, S0_prime_S2_prime_out, S0_prime_S2_prime_S3_prime_out,
       S0_prime_S2S3_out, S0_prime_S2S3_prime_out, S0S1_out, S0S1_prime_out, S0S1_prime_S2_prime_out,
       S0S1_prime_S3_prime_out, S0S1S2_out, S0S1S3_out, S0S2_prime_out, S0S2_prime_S3_prime_out,
       S0S3_prime_out, S1_prime_S2_prime_out, S1_prime_S3_prime_out, S1S2_out, S1S2_prime_out,
       S1S2_prime_S3_out, S1S3_out, S1S3_prime_out, S2_prime_S3_prime_out;

  not not_1 (not_1_out, S0);
  not not_2 (not_2_out, S1);
  not not_3 (not_3_out, S2);
  not not_4 (not_4_out, S3);
  and S1_prime_S2_prime (S1_prime_S2_prime_out, not_2_out, not_3_out);
  and S1_prime_S3_prime (S1_prime_S3_prime_out, not_2_out, not_4_out);
  and S0_prime_S2 (S0_prime_S2_out, not_1_out, S2);
  and S1S3 (S1S3_out, S1, S3);
  and S0S2_prime (S0S2_prime_out, S0, not_3_out);
  and S2_prime_S3_prime (S2_prime_S3_prime_out, not_3_out, not_4_out);
  and S0S3_prime (S0S3_prime_out, S0, not_4_out);
  and S0_prime_S2S3 (S0_prime_S2S3_out, not_1_out, S2, S3);
  and S0_prime_S2_prime (S0_prime_S2_prime_out, not_1_out, not_3_out);
  and S1S2 (S1S2_out, S1, S2);
  and S0S1_prime (S0S1_prime_out, S0, not_2_out);
  and S0_prime_S1_prime_S2 (S0_prime_S1_prime_S2_out, not_1_out, not_2_out, S2);
  and S0_prime_S2S3_prime (S0_prime_S2S3_prime_out, not_1_out, S2, not_4_out);
  and S0S2_prime_S3_prime (S0S2_prime_S3_prime_out, S0, not_3_out, not_4_out);
  and S0S1S3 (S0S1S3_out, S0, S1, S3);
  and S0_prime_S2_prime_S3_prime (S0_prime_S2_prime_S3_prime_out, not_1_out, not_3_out, not_4_out);
  and S0_prime_S1S2_prime (S0_prime_S1S2_prime_out, not_1_out, S1, not_3_out);
  and S0_prime_S1S3_prime (S0_prime_S1S3_prime_out, not_1_out, S1, not_4_out);
  and S0S1_prime_S2_prime (S0S1_prime_S2_prime_out, S0, not_2_out, not_3_out);
  and S0S1_prime_S3_prime (S0S1_prime_S3_prime_out, S0, not_2_out, not_4_out);
  and S0S1S2 (S0S1S2_out, S0, S1, S2);
  and S1S2_prime (S1S2_prime_out, S1, not_3_out);
  and S1S3_prime (S1S3_prime_out, S1, not_4_out);
  and S0S1 (S0S1_out, S0, S1);
  and S1S2_prime_S3 (S1S2_prime_S3_out, S1, not_3_out, S3);
  or or_1 (dR, S0_prime_S2S3_prime_out, S1_prime_S3_prime_out, S0_prime_S1_prime_S2_out, S0S2_prime_S3_prime_out, S0S1S3_out, S1S2_prime_S3_out);
  or or_2 (gR, S0S2_prime_out, S0_prime_S1_prime_S2_out, S1S2_prime_out, S1S3_prime_out, S0S1_out);
  or or_3 (aL_dL_eL_fL, not_1_out, S1_prime_S2_prime_out);
  or or_4 (aR, S1_prime_S3_prime_out, S0_prime_S2_out, S1S3_out, S0S2_prime_out);
  or or_5 (bR, not_2_out, S2_prime_S3_prime_out, S0S2_prime_out, S0S3_prime_out, S0_prime_S2S3_out);
  or or_6 (cR, S3, S0_prime_S2_prime_out, S1S2_out, S0S1_prime_out);
  or or_7 (eR, S1_prime_S3_prime_out, S0_prime_S2S3_prime_out, S0S2_prime_S3_prime_out);
  or or_8 (fR, S0_prime_S2_prime_S3_prime_out, S0_prime_S1S2_prime_out, S0_prime_S1S3_prime_out, S0S1_prime_S2_prime_out, S0S1_prime_S3_prime_out, S0S1S2_out);
endmodule

module _4bit_Bin_Add_Sub_to_7_segs (
  input  ALWAYS_ZERO,
  input  ALWAYS_ONE,
  input  C0,
  input  S,
  input  B0,
  input  A0,
  input  B1,
  input  A1,
  input  B2,
  input  A2,
  input  B3,
  input  A3,
  output S0,
  output S1,
  output S2,
  output S3,
  output C4,
  output OVERFLOW
);

  wire binary_to_7_seg_with_2_displays_1_al_dl_el_fl, binary_to_7_seg_with_2_displays_1_ar,
       binary_to_7_seg_with_2_displays_1_br, binary_to_7_seg_with_2_displays_1_cr,
       binary_to_7_seg_with_2_displays_1_dr, binary_to_7_seg_with_2_displays_1_er,
       binary_to_7_seg_with_2_displays_1_fr, binary_to_7_seg_with_2_displays_1_gr, full_adder_1_carry,
       full_adder_2_carry, full_adder_3_carry, xor_1_out, xor_2_out, xor_3_out, xor_4_out;

  xor xor_1 (xor_1_out, S, B0);
  Full_Adder full_adder_1 (.A(A0), .B(xor_1_out), .C0(C0), .SUM(S0), .CARRY(full_adder_1_carry));
  xor xor_2 (xor_2_out, S, B1);
  Full_Adder full_adder_2 (.A(A1), .B(xor_2_out), .C0(full_adder_1_carry), .SUM(S1), .CARRY(full_adder_2_carry));
  xor xor_3 (xor_3_out, S, B2);
  Full_Adder full_adder_3 (.A(A2), .B(xor_3_out), .C0(full_adder_2_carry), .SUM(S2), .CARRY(full_adder_3_carry));
  xor xor_4 (xor_4_out, S, B3);
  Full_Adder full_adder_4 (.A(A3), .B(xor_4_out), .C0(full_adder_3_carry), .SUM(S3), .CARRY(C4));
  Binary_to_7_seg_with_2_displays binary_to_7_seg_with_2_displays_1 (
    .S0(S3), .S1(S2), .S2(S1), .S3(S0), .aL_dL_eL_fL(binary_to_7_seg_with_2_displays_1_al_dl_el_fl),
    .aR(binary_to_7_seg_with_2_displays_1_ar), .bR(binary_to_7_seg_with_2_displays_1_br),
    .cR(binary_to_7_seg_with_2_displays_1_cr), .dR(binary_to_7_seg_with_2_displays_1_dr),
    .eR(binary_to_7_seg_with_2_displays_1_er), .fR(binary_to_7_seg_with_2_displays_1_fr),
    .gR(binary_to_7_seg_with_2_displays_1_gr));
  xor xor_5 (OVERFLOW, C4, full_adder_3_carry);
  _7_Segment_Display u_7_segment_display_1 (
    .g(ALWAYS_ZERO), .f(binary_to_7_seg_with_2_displays_1_al_dl_el_fl),
    .a(binary_to_7_seg_with_2_displays_1_al_dl_el_fl), .b(ALWAYS_ONE),
    .e(binary_to_7_seg_with_2_displays_1_al_dl_el_fl), .d(binary_to_7_seg_with_2_displays_1_al_dl_el_fl),
    .c(ALWAYS_ONE));  // open: dp
  _7_Segment_Display u_7_segment_display_2 (
    .g(binary_to_7_seg_with_2_displays_1_gr), .f(binary_to_7_seg_with_2_displays_1_fr),
    .a(binary_to_7_seg_with_2_displays_1_ar), .b(binary_to_7_seg_with_2_displays_1_br),
    .e(binary_to_7_seg_with_2_displays_1_er), .d(binary_to_7_seg_with_2_displays_1_dr),
    .c(binary_to_7_seg_with_2_displays_1_cr));  // open: dp

  // Notes on the sheet:
  //   S=0 is adder
  //   S=1 is Subtractor
endmodule
