// Logisim project Lab 13.circ as structural Verilog: 6 circuits, main circuit Full adder
module Full_adder (
  input  Ai,
  input  Bi,
  input  Cin,
  output S,
  output Cout
);

  wire and_1_out, and_2_out, and_3_out;

  ExactlyOne xor_1 (.out(S), .in0(Ai), .in2(Cin), .in4(Bi));
  and and_1 (and_1_out, Ai, Bi);
  and and_2 (and_2_out, Ai, Cin);
  and and_3 (and_3_out, Bi, Cin);
  or or_1 (Cout, and_1_out, and_2_out, and_3_out);
endmodule

module _4_bit_shift_register (
  input  SI,
  input  RESET,
  output SO,
  output out_4
);

  wire clock_1_out, d_ff_1_q, d_ff_2_q, d_ff_3_q;

  Clock clock_1 (.out(clock_1_out));
  D_Flip_Flop d_ff_1 (.clk(clock_1_out), .D(SI), .Q(d_ff_1_q), .reset(RESET));  // open: Qn, preset, en
  D_Flip_Flop d_ff_2 (.clk(clock_1_out), .D(d_ff_1_q), .Q(d_ff_2_q), .reset(RESET));  // open: Qn, preset, en
  D_Flip_Flop d_ff_3 (.clk(clock_1_out), .D(d_ff_2_q), .Q(d_ff_3_q), .reset(RESET));  // open: Qn, preset, en
  D_Flip_Flop d_ff_4 (.clk(clock_1_out), .D(d_ff_3_q), .Q(SO), .Qn(out_4), .reset(RESET));  // open: preset, en
endmodule

module _4_bit_Register_with_D_FF (
  input  RESET,
  input  D0,
  input  D1,
  input  D2,
  input  D3,
  output Q0,
  output Q1,
  output Q2,
  output Q3
);

  wire Clock_out;

  Clock Clock (.out(Clock_out));
  D_Flip_Flop d_ff_1 (.clk(Clock_out), .D(D0), .Q(Q0), .reset(RESET));  // open: Qn, preset, en
  D_Flip_Flop d_ff_2 (.clk(Clock_out), .D(D1), .Q(Q1), .reset(RESET));  // open: Qn, preset, en
  D_Flip_Flop d_ff_3 (.clk(Clock_out), .D(D2), .Q(Q2), .reset(RESET));  // open: Qn, preset, en
  D_Flip_Flop d_ff_4 (.clk(Clock_out), .D(D3), .Q(Q3), .reset(RESET));  // open: Qn, preset, en
endmodule

module _4_bit_register_JK_FF (
  input  D0,
  input  RESET,
  input  D1,
  input  D2,
  input  D3,
  output Q0,
  output Q1,
  output Q2,
  output Q3
);

  wire CLOCK_out, not_1_out, not_2_out, not_3_out, not_4_out;

  Clock CLOCK (.out(CLOCK_out));
  not not_1 (not_1_out, D0);
  not not_2 (not_2_out, D1);
  not not_3 (not_3_out, D2);
  not not_4 (not_4_out, D3);
  J_K_Flip_Flop j_k_ff_1 (.J(D0), .clk(CLOCK_out), .K(not_1_out), .Q(Q0), .reset(RESET));  // open: Qn, preset, en
  J_K_Flip_Flop j_k_ff_2 (.J(D1), .clk(CLOCK_out), .K(not_2_out), .Q(Q1), .reset(RESET));  // open: Qn, preset, en
  J_K_Flip_Flop j_k_ff_3 (.J(D2), .clk(CLOCK_out), .K(not_3_out), .Q(Q2), .reset(RESET));  // open: Qn, preset, en
  J_K_Flip_Flop j_k_ff_4 (.J(D3), .clk(CLOCK_out), .K(not_4_out), .Q(Q3), .reset(RESET));  // open: Qn, preset, en
endmodule

module _4_bit_Register_with_Parallel_Load (
  input  LOAD,
  input  LOAD_2,
  input  D0,
  input  D0_2,
  input  D1,
  input  D1_2,
  input  D2,
  input  D2_2,
  input  D3,
  input  D3_2,
  output Q0,
  output Q0_2,
  output Q1,
  output Q1_2,
  output Q2,
  output Q2_2,
  output Q3,
  output Q3_2
);

  wire and_1_out, and_2_out, and_3_out, and_4_out, and_5_out, and_6_out, and_7_out, and_8_out, Clock_2_out,
       Clock_out, not_1_out, not_2_out, or_1_out, or_2_out, or_3_out, or_4_out, or_5_out;

  not not_1 (not_1_out, LOAD);
  Clock Clock (.out(Clock_out));
  or or_1 (or_1_out, not_1_out, Clock_out);
  D_Flip_Flop d_ff_1 (.clk(or_1_out), .D(D0_2), .Q(Q0_2));  // open: Qn, preset, en, reset
  D_Flip_Flop d_ff_2 (.clk(or_1_out), .D(D1_2), .Q(Q1_2));  // open: Qn, preset, en, reset
  D_Flip_Flop d_ff_3 (.clk(or_1_out), .D(D2_2), .Q(Q2_2));  // open: Qn, preset, en, reset
  D_Flip_Flop d_ff_4 (.clk(or_1_out), .D(D3_2), .Q(Q3_2));  // open: Qn, preset, en, reset
  not not_2 (not_2_out, LOAD_2);
  Clock Clock_2 (.out(Clock_2_out));
  and and_1 (and_1_out, LOAD_2, D0);
  and and_2 (and_2_out, D0, not_2_out);
  and and_3 (and_3_out, LOAD_2, D1);
  and and_4 (and_4_out, not_2_out, D1);
  and and_5 (and_5_out, LOAD_2, D2);
  and and_6 (and_6_out, D2, not_2_out);
  and and_7 (and_7_out, LOAD_2, D3);
  and and_8 (and_8_out, not_2_out, D3);
  or or_2 (or_2_out, and_1_out, and_2_out);
  or or_3 (or_3_out, and_3_out, and_4_out);
  or or_4 (or_4_out, and_5_out, and_6_out);
  or or_5 (or_5_out, and_7_out, and_8_out);
  D_Flip_Flop d_ff_5 (.clk(Clock_2_out), .D(or_2_out), .Q(Q0));  // open: Qn, preset, en, reset
  D_Flip_Flop d_ff_6 (.clk(Clock_2_out), .D(or_3_out), .Q(Q1));  // open: Qn, preset, en, reset
  D_Flip_Flop d_ff_7 (.clk(Clock_2_out), .D(or_4_out), .Q(Q2));  // open: Qn, preset, en, reset
  D_Flip_Flop d_ff_8 (.clk(Clock_2_out), .D(or_5_out), .Q(Q3));  // open: Qn, preset, en, reset

  // Notes on the sheet:
  //   Not Truly Synchronous
  //   Synchronous
endmodule

module Serial_Addition_systems (
  input  RESET,
  input  Shift,
  input  SIB,
  input  RESET_2,
  input  Load,
  input  Load_2,
  output out_7,
  output out_8,
  output out_9,
  output out_10,
  output out_11,
  output out_12,
  output out_13,
  output out_14,
  output out_15,
  output out_16
);

  wire CLOCK_2_out, Clock_3_out, Clock_out, d_ff_1_q, d_ff_2_q, d_ff_3_q, d_ff_4_q, d_ff_5_q, d_ff_6_q,
       d_ff_7_q, d_ff_8_q, d_ff_9_q, d_ff_10_q, d_ff_11_q, d_ff_12_q, d_ff_13_q, d_ff_14_q, d_ff_15_q,
       d_ff_16_q, d_ff_17_q, d_ff_18_q, d_ff_19_q, d_ff_20_q, d_ff_21_q, full_adder_1_cout, full_adder_1_s,
       full_adder_2_cout, full_adder_2_s, full_adder_3_cout, full_adder_3_s, full_adder_4_cout,
       full_adder_4_s, full_adder_5_cout, full_adder_5_s, not_1_out, not_2_out, not_3_out, or_1_out,
       or_2_out, or_3_out;

  Clock Clock (.out(Clock_out));
  not not_1 (not_1_out, Shift);
  Clock CLOCK_2 (.out(CLOCK_2_out));
  not not_2 (not_2_out, Load);
  or or_1 (or_1_out, not_1_out, CLOCK_2_out);
  or or_2 (or_2_out, not_2_out, Clock_out);
  D_Flip_Flop d_ff_1 (.clk(or_2_out), .D(full_adder_1_s), .Q(d_ff_1_q), .Qn(out_9));  // open: preset, en, reset
  D_Flip_Flop d_ff_2 (.clk(or_2_out), .D(full_adder_2_s), .Q(d_ff_2_q), .Qn(out_11));  // open: preset, en, reset
  D_Flip_Flop d_ff_3 (.clk(or_2_out), .D(full_adder_3_s), .Q(d_ff_3_q), .Qn(out_13));  // open: preset, en, reset
  D_Flip_Flop d_ff_4 (.clk(or_2_out), .D(full_adder_4_s), .Q(d_ff_4_q), .Qn(out_15));  // open: preset, en, reset
  D_Flip_Flop d_ff_5 (.clk(or_1_out), .D(full_adder_5_s), .Q(d_ff_5_q), .reset(RESET));  // open: Qn, preset, en
  D_Flip_Flop d_ff_6 (.clk(or_1_out), .D(SIB), .Q(d_ff_6_q), .reset(RESET_2));  // open: Qn, preset, en
  Clock Clock_3 (.out(Clock_3_out));
  D_Flip_Flop d_ff_7 (.clk(or_1_out), .D(d_ff_5_q), .Q(d_ff_7_q), .reset(RESET));  // open: Qn, preset, en
  D_Flip_Flop d_ff_8 (.clk(or_1_out), .D(d_ff_6_q), .Q(d_ff_8_q), .reset(RESET_2));  // open: Qn, preset, en
  not not_3 (not_3_out, Load_2);
  or or_3 (or_3_out, not_3_out, Clock_3_out);
  D_Flip_Flop d_ff_9 (.clk(or_1_out), .D(d_ff_7_q), .Q(d_ff_9_q), .reset(RESET));  // open: Qn, preset, en
  D_Flip_Flop d_ff_10 (.clk(or_1_out), .D(d_ff_8_q), .Q(d_ff_10_q), .reset(RESET_2));  // open: Qn, preset, en
  D_Flip_Flop d_ff_11 (.clk(or_1_out), .D(d_ff_9_q), .Q(d_ff_11_q), .Qn(out_7), .reset(RESET));  // open: preset, en
  D_Flip_Flop d_ff_12 (.clk(or_1_out), .D(d_ff_10_q), .Q(d_ff_12_q), .Qn(out_8), .reset(RESET_2));  // open: preset, en
  D_Flip_Flop d_ff_13 (.clk(or_3_out), .D(full_adder_1_s), .Q(d_ff_13_q), .Qn(out_10));  // open: preset, en, reset
  D_Flip_Flop d_ff_14 (.clk(or_3_out), .D(full_adder_2_s), .Q(d_ff_14_q), .Qn(out_12));  // open: preset, en, reset
  D_Flip_Flop d_ff_15 (.clk(or_3_out), .D(full_adder_3_s), .Q(d_ff_15_q), .Qn(out_14));  // open: preset, en, reset
  D_Flip_Flop d_ff_16 (.clk(or_3_out), .D(full_adder_4_s), .Q(d_ff_16_q), .Qn(out_16));  // open: preset, en, reset
  Full_adder full_adder_1 (
    .Ai(d_ff_1_q), .Bi(d_ff_13_q), .Cin(d_ff_17_q), .S(full_adder_1_s), .Cout(full_adder_1_cout));
  D_Flip_Flop d_ff_17 (.clk(or_3_out), .D(full_adder_1_cout), .Q(d_ff_17_q));  // open: Qn, preset, en, reset
  Full_adder full_adder_2 (
    .Ai(d_ff_2_q), .Bi(d_ff_14_q), .Cin(d_ff_20_q), .S(full_adder_2_s), .Cout(full_adder_2_cout));
  Full_adder full_adder_3 (
    .Ai(d_ff_3_q), .Bi(d_ff_15_q), .Cin(d_ff_21_q), .S(full_adder_3_s), .Cout(full_adder_3_cout));
  Full_adder full_adder_4 (
    .Ai(d_ff_4_q), .Bi(d_ff_16_q), .Cin(d_ff_18_q), .S(full_adder_4_s), .Cout(full_adder_4_cout));
  D_Flip_Flop d_ff_18 (.clk(or_3_out), .D(full_adder_4_cout), .Q(d_ff_18_q));  // open: Qn, preset, en, reset
  Full_adder full_adder_5 (
    .Ai(d_ff_11_q), .Bi(d_ff_12_q), .Cin(d_ff_19_q), .S(full_adder_5_s), .Cout(full_adder_5_cout));
  D_Flip_Flop d_ff_19 (.clk(or_1_out), .D(full_adder_5_cout), .Q(d_ff_19_q));  // open: Qn, preset, en, reset
  D_Flip_Flop d_ff_20 (.clk(or_3_out), .D(full_adder_2_cout), .Q(d_ff_20_q));  // open: Qn, preset, en, reset
  D_Flip_Flop d_ff_21 (.clk(or_3_out), .D(full_adder_3_cout), .Q(d_ff_21_q));  // open: Qn, preset, en, reset

  // Notes on the sheet:
  //   with normal registers
  //   Register A
  //   with Shift Register
  //   SHIFT REGISTER A
  //   SHIFT REGISTER B
  //   Register B
endmodule
