// Logisim project Lab 9.circ as structural Verilog: 8 circuits, main circuit Lab9 decoders
module Lab9_decoders (
  input  in_1,
  input  in_2,
  input  in_3,
  input  in_4,
  input  [1:0] in_5,
  input  in_6,
  input  in_7,
  input  in_8,
  input  [2:0] in_9
);

  wire and_1_out, and_2_out, and_3_out, and_4_out, and_5_out, and_6_out, and_7_out, and_8_out, and_9_out,
       and_10_out, and_11_out, and_12_out, decoder_1_out0, decoder_1_out1, decoder_1_out2, decoder_1_out3,
       decoder_1_out4, decoder_1_out5, decoder_1_out6, decoder_1_out7, decoder_2_out0, decoder_2_out1,
       decoder_3_out0, decoder_3_out1, decoder_3_out2, decoder_3_out3, not_1_out, not_2_out, not_3_out,
       not_4_out, not_5_out, not_6_out, not_7_out, not_8_out, not_9_out, not_10_out, not_11_out, not_12_out,
       not_13_out, not_14_out, not_15_out, not_16_out, not_17_out;

  Decoder #(.select(3)) decoder_1 (
    .out0(decoder_1_out0), .out1(decoder_1_out1), .out2(decoder_1_out2), .out3(decoder_1_out3),
    .out4(decoder_1_out4), .out5(decoder_1_out5), .out6(decoder_1_out6), .out7(decoder_1_out7), .sel(in_9));  // open: en
  LED led_1 (.in(decoder_2_out0));
  LED led_2 (.in(decoder_2_out1));
  Decoder decoder_2 (.out0(decoder_2_out0), .out1(decoder_2_out1), .sel(in_2), .en(1'b1));
  LED led_3 (.in(decoder_3_out0));
  LED led_4 (.in(decoder_3_out1));
  LED led_5 (.in(decoder_3_out2));
  Decoder #(.select(2)) decoder_3 (
    .out0(decoder_3_out0), .out1(decoder_3_out1), .out2(decoder_3_out2), .out3(decoder_3_out3), .sel(in_5));  // open: en
  LED led_6 (.in(decoder_3_out3));
  LED led_7 (.in(decoder_1_out0));
  LED led_8 (.in(decoder_1_out1));
  LED led_9 (.in(decoder_1_out2));
  LED led_10 (.in(decoder_1_out3));
  LED led_11 (.in(decoder_1_out4));
  LED led_12 (.in(decoder_1_out5));
  LED led_13 (.in(decoder_1_out6));
  LED led_14 (.in(decoder_1_out7));
  not not_1 (not_1_out, in_3);
  not not_2 (not_2_out, in_4);
  not not_3 (not_3_out, in_3);
  not not_4 (not_4_out, in_4);
  not not_5 (not_5_out, in_6);
  not not_6 (not_6_out, in_7);
  not not_7 (not_7_out, in_8);
  not not_8 (not_8_out, in_6);
  not not_9 (not_9_out, in_7);
  not not_10 (not_10_out, in_6);
  not not_11 (not_11_out, in_8);
  not not_12 (not_12_out, in_6);
  not not_13 (not_13_out, in_7);
  not not_14 (not_14_out, in_8);
  not not_15 (not_15_out, in_7);
  not not_16 (not_16_out, in_8);
  LED led_15 (.in(not_17_out));
  not not_17 (not_17_out, in_1);
  LED led_16 (.in(in_1));
  and and_1 (and_1_out, not_1_out, not_2_out);
  LED led_17 (.in(and_1_out));
  and and_2 (and_2_out, not_3_out, in_4);
  LED led_18 (.in(and_2_out));
  and and_3 (and_3_out, in_3, not_4_out);
  LED led_19 (.in(and_3_out));
  LED led_20 (.in(and_4_out));
  and and_4 (and_4_out, in_3, in_4);
  LED led_21 (.in(and_5_out));
  and and_5 (and_5_out, not_5_out, not_6_out, not_7_out);
  LED led_22 ();  // open: in
  and and_6 (and_6_out, not_8_out, not_9_out, in_8);
  LED led_23 (.in(and_6_out));
  and and_7 (and_7_out, not_10_out, in_7, not_11_out);
  LED led_24 (.in(and_7_out));
  and and_8 (and_8_out, not_12_out, in_7, in_8);
  LED led_25 (.in(and_8_out));
  LED led_26 (.in(and_9_out));
  and and_9 (and_9_out, in_6, not_13_out, not_14_out);
  and and_10 (and_10_out, in_6, not_15_out, in_8);
  LED led_27 (.in(and_10_out));
  and and_11 (and_11_out, in_6, in_7, not_16_out);
  LED led_28 (.in(and_11_out));
  and and_12 (and_12_out, in_6, in_7, in_8);
  LED led_29 (.in(and_12_out));

  // Notes on the sheet:
  //   3:8 decoder
  //   1:2 decoder
  //   2:4 decoder
  //   1:2 decoeder with basic gates
  //   N not gates    2^N and gates
  //   2:4 decoder with basic gates
  //   3:8 decoder with basic gates
endmodule

module _9_1_function_to_multiplexer (
  input  D,
  input  _0,
  input  _1,
  input  [2:0] A_B_C,
  output out_5
);

  wire not_1_out;

  not not_1 (not_1_out, D);
  Multiplexer #(.select(3)) multiplexer_1 (
    .in0(not_1_out), .in1(not_1_out), .in2(D), .in3(_1), .in4(not_1_out), .in5(not_1_out), .in6(_0),
    .in7(_0), .out(out_5), .sel(A_B_C));  // open: en
  // NOT_Gate not_2 is placed but not wired

  // Notes on the sheet:
  //   Question 1: Implement the function into a multiplexer with NOT gate
  //   F(A,B,C,D) = (A'+B'+D)(A'+D')(A+B+D')(A+B'+C+D)
endmodule

module _9_2_multiplexer_using_decoder (
  input  [1:0] S1_S2,
  input  I3,
  input  I2,
  input  I1,
  input  I0,
  output out_6
);

  wire and_1_out, and_2_out, and_3_out, and_4_out, decoder_1_out0, decoder_1_out1, decoder_1_out2,
       decoder_1_out3;

  Decoder #(.select(2)) decoder_1 (
    .out0(decoder_1_out0), .out1(decoder_1_out1), .out2(decoder_1_out2), .out3(decoder_1_out3), .sel(S1_S2));  // open: en
  and and_1 (and_1_out, I3, decoder_1_out3);
  and and_2 (and_2_out, I2, decoder_1_out2);
  and and_3 (and_3_out, I1, decoder_1_out1);
  and and_4 (and_4_out, I0, decoder_1_out0);
  or or_1 (out_6, and_1_out, and_2_out, and_3_out, and_4_out);

  // Notes on the sheet:
  //   Question 2: design a 4-1 multiplexer using a decoder
endmodule

module _9_3_MUX___inverter (
  input  D,
  input  _0,
  input  _1,
  input  [2:0] in_4,
  output F
);

  wire not_1_out;

  not not_1 (not_1_out, D);
  Multiplexer #(.select(3)) multiplexer_1 (
    .in0(_0), .in1(not_1_out), .in2(not_1_out), .in3(not_1_out), .in4(D), .in5(_1), .in6(_0), .in7(D),
    .out(F), .sel(in_4));  // open: en

  // Notes on the sheet:
  //   F(ABCD)= m2 + m4 + m6 + m9 + m10 + m11 + m15
endmodule

module _9_4_8_to_1_MUX (
  input  [2:0] S1_S2_S3,
  input  I7,
  input  I6,
  input  I5,
  input  I4,
  input  I3,
  input  I2,
  input  I1,
  input  I0,
  output F
);

  wire and_1_out, and_2_out, and_3_out, and_4_out, and_5_out, and_6_out, and_7_out, and_8_out,
       decoder_1_out0, decoder_1_out1, decoder_1_out2, decoder_1_out3, decoder_1_out4, decoder_1_out5,
       decoder_1_out6, decoder_1_out7;

  Decoder #(.select(3)) decoder_1 (
    .out0(decoder_1_out0), .out1(decoder_1_out1), .out2(decoder_1_out2), .out3(decoder_1_out3),
    .out4(decoder_1_out4), .out5(decoder_1_out5), .out6(decoder_1_out6), .out7(decoder_1_out7), .sel(S1_S2_S3));  // open: en
  and and_1 (and_1_out, decoder_1_out7, I7);
  and and_2 (and_2_out, decoder_1_out6, I6);
  and and_3 (and_3_out, decoder_1_out5, I5);
  and and_4 (and_4_out, decoder_1_out4, I4);
  and and_5 (and_5_out, decoder_1_out3, I3);
  and and_6 (and_6_out, decoder_1_out2, I2);
  and and_7 (and_7_out, decoder_1_out1, I1);
  and and_8 (and_8_out, decoder_1_out0, I0);
  or or_1 (F, and_1_out, and_2_out, and_3_out, and_4_out, and_5_out, and_6_out, and_7_out, and_8_out);
endmodule

module _9_5_8to1_MUX_from_two_4_1MUX_and_one_2_1_MUX (
  input  I0,
  input  I1,
  input  I2,
  input  I3,
  input  [1:0] S0_S1,
  input  I4,
  input  I5,
  input  S2,
  input  I6,
  input  I7,
  output out_11
);

  wire multiplexer_1_out, multiplexer_2_out;

  Multiplexer #(.select(2)) multiplexer_1 (
    .in0(I0), .in1(I1), .in2(I2), .in3(I3), .out(multiplexer_1_out), .sel(S0_S1));  // open: en
  Multiplexer #(.select(2)) multiplexer_2 (
    .in0(I4), .in1(I5), .in2(I6), .in3(I7), .out(multiplexer_2_out), .sel(S0_S1));  // open: en
  Multiplexer multiplexer_3 (.in0(multiplexer_1_out), .in1(multiplexer_2_out), .out(out_11), .sel(S2));  // open: en

  // Notes on the sheet:
  //   8:1 MUX out of two 4:1 MUX and one 2:1 MUX
endmodule

module _9_7_MUX_with_AND_and_OR (
  input  A,
  input  B,
  input  S,
  output out_4
);

  wire and_1_out, or_1_out;

  or or_1 (or_1_out, A, B);
  and and_1 (and_1_out, A, B);
  Multiplexer multiplexer_1 (.in0(or_1_out), .in1(and_1_out), .out(out_4), .sel(S));  // open: en

  // Notes on the sheet:
  //   7) Design a multiplexer that allows one of a number of operations to be chosen and applied to the inputs (AND & OR gates
endmodule

module _9_8_Comparator (
  input  [1:0] A3__B3,
  input  [1:0] A2__B2,
  input  [1:0] A1__B1,
  input  [1:0] A0__B0
);

  wire decoder_1_out0, decoder_1_out1, decoder_1_out2, decoder_1_out3, decoder_2_out0, decoder_2_out1,
       decoder_2_out2, decoder_2_out3, decoder_3_out0, decoder_3_out1, decoder_3_out2, decoder_3_out3,
       decoder_4_out0, decoder_4_out1, decoder_4_out2, decoder_4_out3, or_1_out, or_2_out, or_3_out, or_4_out;

  Decoder #(.select(2)) decoder_1 (
    .out0(decoder_1_out0), .out1(decoder_1_out1), .out2(decoder_1_out2), .out3(decoder_1_out3), .sel(A3__B3));  // open: en
  LED led (.in(decoder_1_out1));
  or or_1 (or_1_out, decoder_1_out3, decoder_1_out0);
  LED led_2 (.in(decoder_1_out2));
  Decoder #(.select(2)) decoder_2 (
    .out0(decoder_2_out0), .out1(decoder_2_out1), .out2(decoder_2_out2), .out3(decoder_2_out3), .sel(A2__B2),
    .en(or_1_out));
  LED led_3 (.in(decoder_2_out1));
  or or_2 (or_2_out, decoder_2_out3, decoder_2_out0);
  LED led_4 (.in(decoder_2_out2));
  Decoder #(.select(2)) decoder_3 (
    .out0(decoder_3_out0), .out1(decoder_3_out1), .out2(decoder_3_out2), .out3(decoder_3_out3), .sel(A1__B1),
    .en(or_2_out));
  LED led_5 (.in(decoder_3_out1));
  or or_3 (or_3_out, decoder_3_out3, decoder_3_out0);
  LED led_6 (.in(decoder_3_out2));
  Decoder #(.select(2)) decoder_4 (
    .out0(decoder_4_out0), .out1(decoder_4_out1), .out2(decoder_4_out2), .out3(decoder_4_out3), .sel(A0__B0),
    .en(or_3_out));
  LED led_7 (.in(decoder_4_out1));
  LED led_8 (.in(decoder_4_out2));
  LED led_9 (.in(or_4_out));
  or or_4 (or_4_out, decoder_4_out3, decoder_4_out0);

  // Notes on the sheet:
  //   Making a 4 bit comparator out of four 2:4 decoders
  //   PLEASE NOTE: for some reason when certain binary are activated in the multibit inputs, parts of the circuit may become blue or red
  //   However, the circuit still works as intended. I am unsure why it acts as such, but I left it as is since it still works
endmodule
