// Logisim project Lab5.circ as structural Verilog: 9 circuits, main circuit LAB 5--1.1
module LAB_5__1_1 (
  input  A,
  input  B,
  input  C,
  input  in_4,
  output out_5,
  output out_6
);

  wire and_1_out, and_2_out, and_3_out, and_4_out, and_5_out, not_1_out, not_2_out, not_3_out, not_4_out,
       or_1_out;

  not not_1 (not_1_out, B);
  and and_1 (and_1_out, A, not_1_out, C);
  and and_2 (and_2_out, not_1_out, not_3_out);
  not not_2 (not_2_out, A);
  not not_3 (not_3_out, C);
  not not_4 (not_4_out, A);
  and and_3 (and_3_out, not_2_out, C);
  and and_4 (and_4_out, B, not_3_out, not_4_out);
  and and_5 (and_5_out, A, B);
  or or_1 (or_1_out, and_1_out, and_2_out, and_3_out, and_4_out);
  or or_2 (out_5, or_1_out, and_5_out);

  assign out_6 = in_4;

  // Notes on the sheet:
  //   AB'C
  //   Logic Circuit after K-Map Simplified:
  //   Logic Circuit before K-map Simplification: F(A,B,C) = AB'C+B'C'+A'C+A'BC'+AB
  //   B'C'
  //   A'C
  //   Note: K-map shows that the above always outputs 1 regardless of input
  //   A'BC'
  //   AB'C+B'C'+A'C+A'BC'
  //   AB
  //   F = AB'C+B'C'+A'C+A'BC'+AB
endmodule

module Lab_5___1_2 (
  input  A,
  input  B,
  input  C,
  input  D,
  input  A_2,
  input  B_2,
  input  C_2,
  input  D_2,
  output F,
  output F_A_prime_B_prime_C_prime_D
);

  wire and_1_out, and_2_out, and_3_out, and_4_out, and_5_out, and_6_out, not_1_out, not_2_out, not_3_out,
       not_4_out, not_5_out, not_6_out, or_2_out, or_3_out;

  not not_1 (not_1_out, B_2);
  not not_2 (not_2_out, C_2);
  not not_3 (not_3_out, A);
  not not_4 (not_4_out, B);
  not not_5 (not_5_out, C);
  not not_6 (not_6_out, A_2);
  and and_1 (and_1_out, not_2_out, D_2);
  or or_1 (F_A_prime_B_prime_C_prime_D, not_6_out, not_1_out, and_1_out);
  and and_2 (and_2_out, not_3_out, B);
  and and_3 (and_3_out, A, not_4_out, not_5_out, D);
  and and_4 (and_4_out, not_4_out, C, D);
  and and_5 (and_5_out, not_5_out, D);
  or or_2 (or_2_out, and_2_out, and_3_out, and_4_out, and_5_out);
  and and_6 (and_6_out, A, not_5_out, D);
  or or_3 (or_3_out, not_4_out, and_6_out);
  or or_4 (F, or_2_out, or_3_out);

  // Notes on the sheet:
  //   A'
  //   B'
  //   C'D
  //   Logic Circuit after K-map Simplification: F=A'+C'D+B'
  //   Logic Circuit before K-map Simplification: F(A,B,C,D) = A'B+AB'C'D+B'CD+C'D+B'+AC'D
  //   A'B
  //   AB'C'D
  //   B'CD
  //   B'
  //   C'D
  //   AC'D
  //   A'B+AB'C'D+B'CD+C'D
  //   B'+AC'D
endmodule

module Lab_5___1_3 (
  input  A,
  input  B,
  input  C,
  input  D,
  input  A_2,
  input  B_2,
  input  C_2,
  input  D_2,
  output F,
  output F_A_prime_D_BD_ABC
);

  wire and_1_out, and_2_out, and_3_out, and_4_out, and_5_out, and_6_out, and_7_out, and_8_out, not_1_out,
       not_2_out, not_3_out, not_4_out;

  not not_1 (not_1_out, A_2);
  not not_2 (not_2_out, A);
  not not_3 (not_3_out, B);
  not not_4 (not_4_out, C);
  and and_1 (and_1_out, not_1_out, D_2);
  and and_2 (and_2_out, B_2, D_2, C_2);
  and and_3 (and_3_out, A_2, B_2, C_2);
  and and_4 (and_4_out, not_2_out, B, not_4_out, D);
  and and_5 (and_5_out, not_2_out, not_3_out, D);
  and and_6 (and_6_out, not_2_out, C, D);
  and and_7 (and_7_out, A, B, D);
  and and_8 (and_8_out, A, B, C);
  or or_1 (F_A_prime_D_BD_ABC, and_1_out, and_2_out, and_3_out);
  or or_2 (F, and_4_out, and_5_out, and_6_out, and_7_out, and_8_out);

  // Notes on the sheet:
  //   Logic Circuit after k-map simplification:
  //   A'D
  //   BD
  //   ABC
  //   Logic Circuit before K-map simplification: F=A'BC'D+A'B'D+A'CD+ABD+ABC
  //   A'BC'D
  //   A'B'D
  //   A'CD
  //   ABD
  //   ABC
endmodule

module Lab_5___1_4 (
  input  A,
  input  B,
  input  C,
  input  D,
  input  A_2,
  input  B_2,
  input  C_2,
  input  D_2,
  output F,
  output out_10
);

  wire and_1_out, and_2_out, and_3_out, and_4_out, and_5_out, and_6_out, and_7_out, and_8_out, and_9_out,
       and_10_out, and_11_out, and_12_out, and_13_out, and_14_out, not_1_out, not_2_out, not_3_out,
       not_4_out, not_5_out, not_8_out, not_9_out, not_10_out, not_11_out, not_12_out, or_2_out, or_3_out;

  not not_1 (not_1_out, A);
  not not_2 (not_2_out, A);
  not not_3 (not_3_out, A_2);
  not not_4 (not_4_out, B_2);
  not not_5 (not_5_out, C_2);
  not not_6 (not_1_out, B);
  not not_7 (not_1_out, C);
  not not_8 (not_8_out, D);
  not not_9 (not_9_out, C);
  not not_10 (not_10_out, D);
  not not_11 (not_11_out, B);
  and and_1 (and_1_out, not_3_out, D_2);
  and and_2 (and_2_out, not_3_out, not_4_out, not_5_out);
  not not_12 (not_12_out, D_2);
  and and_3 (and_3_out, not_1_out, not_1_out, not_1_out, not_8_out);
  and and_4 (and_4_out, not_1_out, not_1_out, not_1_out, D);
  and and_5 (and_5_out, not_1_out, not_1_out, C, D);
  and and_6 (and_6_out, not_4_out, C_2, D_2);
  and and_7 (and_7_out, not_3_out, B_2, C_2);
  and and_8 (and_8_out, not_1_out, B, not_1_out, D);
  and and_9 (and_9_out, not_2_out, B, C, D);
  and and_10 (and_10_out, not_2_out, B, C, not_8_out);
  and and_11 (and_11_out, A, B, not_9_out, not_10_out);
  and and_12 (and_12_out, A, B, C, not_10_out);
  and and_13 (and_13_out, A, not_11_out, C, D);
  and and_14 (and_14_out, A_2, B_2, not_12_out);
  or or_1 (out_10, and_1_out, and_2_out, and_6_out, and_7_out, and_14_out);
  or or_2 (or_2_out, and_3_out, and_4_out, and_5_out, and_8_out);
  or or_3 (or_3_out, and_9_out, and_10_out, and_11_out, and_12_out, and_13_out);
  or or_4 (F, or_2_out, or_3_out);

  // Notes on the sheet:
  //   a'b'c'd'
  //   a'b'c'd
  //   Logic Circuit after k-map simplification:
  //   a'd
  //   a'b'c'
  //   b'cd
  //   Logic Circuit before k-map simplification: f(a,b,c,d)= (symbol for minterms) Em(0,1,3,5,6,7,11,12,14)
  //   a'b'cd
  //   a'bc'd
  //   a'bcd
  //   a'bcd'
  //   abc'd'
  //   abc'd
  //   ab'cd
  //   a'bc
  //   abd'
  //   a'b'c'd'+a'b'c'd+a'b'cd+a'bc'd
  //   f=a'd+a'b'c'+b'cd+a'bc+abd'
  //   a'bcd+a'bcd'+abc'd'+abc'd+ab'cd
endmodule

module Lab_5__1_5 (
  input  A,
  input  B,
  input  C,
  input  A_2,
  input  B_2,
  input  C_2,
  output f1,
  output f1_A_prime_BC_prime_AC_B_prime_C
);

  wire and_1_out, and_2_out, and_3_out, and_4_out, and_5_out, and_6_out, and_7_out, not_1_out, not_2_out,
       not_3_out, not_4_out, not_5_out, not_6_out, not_7_out;

  not not_1 (not_1_out, A);
  not not_2 (not_2_out, A);
  not not_3 (not_3_out, C);
  not not_4 (not_4_out, A);
  not not_5 (not_5_out, A_2);
  not not_6 (not_6_out, C_2);
  and and_1 (and_1_out, not_1_out, not_2_out, C);
  and and_2 (and_2_out, not_1_out, A, not_3_out);
  and and_3 (and_3_out, A, A, C);
  and and_4 (and_4_out, A, not_4_out, C);
  and and_5 (and_5_out, not_5_out, B_2, not_6_out);
  and and_6 (and_6_out, A_2, C_2);
  not not_7 (not_7_out, B_2);
  and and_7 (and_7_out, not_7_out, C_2);
  or or_1 (f1, and_1_out, and_2_out, and_3_out, and_4_out);
  or or_2 (f1_A_prime_BC_prime_AC_B_prime_C, and_5_out, and_6_out, and_7_out);

  assign B = A;

  // Notes on the sheet:
  //   Logic circuit before k-map simplification: f1(A,B,C) = m1+m2+m5+m7
  //   A'B'C
  //   A'BC'
  //   ABC
  //   AB'C
  //   Logic Circuit after k-map simplification:
  //   A'BC'
  //   AC
  //   B'C
endmodule

module Lab_5___1_6 (
  input  d,
  input  e,
  input  f,
  input  d_2,
  input  e_2,
  input  f_2,
  output f2,
  output f2_df_de_prime_e_prime_f
);

  wire and_1_out, and_2_out, and_3_out, and_4_out, and_5_out, and_6_out, and_7_out, not_1_out, not_2_out,
       not_3_out, not_4_out;

  not not_1 (not_1_out, d);
  not not_2 (not_2_out, e);
  not not_3 (not_3_out, e_2);
  not not_4 (not_4_out, f);
  and and_1 (and_1_out, d_2, f_2);
  and and_2 (and_2_out, not_1_out, not_2_out, f);
  and and_3 (and_3_out, d, e, f);
  and and_4 (and_4_out, d, not_2_out, not_4_out);
  and and_5 (and_5_out, d_2, not_3_out);
  and and_6 (and_6_out, not_3_out, f_2);
  and and_7 (and_7_out, d, not_2_out, f);
  or or_1 (f2_df_de_prime_e_prime_f, and_1_out, and_5_out, and_6_out);
  or or_2 (f2, and_2_out, and_3_out, and_4_out, and_7_out);

  // Notes on the sheet:
  //   def
  //   de'f'
  //   Logic circuit after k-map simplification:
  //   df
  //   de'
  //   e'f
  //   Logic Circuit before k-map simplification: f2(d,e,f)=(symbol for minterms)Em(1,4,5,7)
  //   d'e'f
  //   de'f
endmodule

module LAB_5__2 (
  input  A,
  input  B,
  input  C,
  input  D,
  input  A_2,
  input  B_2,
  input  C_2,
  input  D_2,
  output F,
  output F_A_BC_CD
);

  wire A_prime_B_prime_CD_out, A_prime_BCD_out, A_prime_BCD_prime_out, AB_prime_C_prime_D_out,
       AB_prime_C_prime_D_prime_out, AB_prime_CD_out, AB_prime_CD_prime_out, ABC_prime_D_out,
       ABC_prime_D_prime_out, ABCD_out, ABCD_prime_out, and_1_out, and_2_out, not_1_out, not_2_out,
       not_3_out, not_4_out, or_2_out, or_3_out, or_4_out;

  not not_1 (not_1_out, A);
  not not_2 (not_2_out, B);
  not not_3 (not_3_out, C);
  not not_4 (not_4_out, D);
  and A_prime_B_prime_CD (A_prime_B_prime_CD_out, not_1_out, C, D, not_2_out);
  and and_1 (and_1_out, B_2, C_2);
  and and_2 (and_2_out, C_2, D_2);
  and A_prime_BCD (A_prime_BCD_out, not_1_out, B, C, D);
  or or_1 (F_A_BC_CD, A_2, and_1_out, and_2_out);
  and AB_prime_C_prime_D (AB_prime_C_prime_D_out, A, not_2_out, not_3_out, D);
  and AB_prime_CD (AB_prime_CD_out, A, not_2_out, C, D);
  and ABC_prime_D_prime (ABC_prime_D_prime_out, A, B, not_3_out, not_4_out);
  and A_prime_BCD_prime (A_prime_BCD_prime_out, not_1_out, B, C, not_4_out);
  and ABC_prime_D (ABC_prime_D_out, A, B, not_3_out, D);
  and AB_prime_C_prime_D_prime (AB_prime_C_prime_D_prime_out, A, not_2_out, not_4_out, not_3_out);
  and AB_prime_CD_prime (AB_prime_CD_prime_out, A, not_2_out, C, not_4_out);
  and ABCD_prime (ABCD_prime_out, A, B, not_4_out, C);
  or or_2 (or_2_out, A_prime_B_prime_CD_out, A_prime_BCD_prime_out, A_prime_BCD_out, AB_prime_C_prime_D_prime_out);
  or or_3 (or_3_out, AB_prime_C_prime_D_out, AB_prime_CD_prime_out, AB_prime_CD_out, ABC_prime_D_prime_out, ABC_prime_D_out);
  and ABCD (ABCD_out, A, B, C, D);
  or or_4 (or_4_out, ABCD_prime_out, ABCD_out);
  or or_5 (F, or_2_out, or_3_out, or_4_out);

  // Notes on the sheet:
  //   #2: Logic circuit before k-map simplification
  //   Logic circuit after k-map simplification:
  //   BC
  //   CD
  //   AB'C'D+AB'CD'+AB'CD+ABC'D'+ABC'D
  //   A'B'CD+A'BCD'+A'BCD+AB'C'D'
  //   ABCD'+ABCD
endmodule

module Lab_5___3 (
  input  A,
  input  B,
  input  C,
  output F_A_prime_C_prime_B_prime
);

  wire and_1_out, not_1_out, not_2_out, not_3_out;

  not not_1 (not_1_out, A);
  not not_2 (not_2_out, C);
  and and_1 (and_1_out, not_1_out, not_2_out);
  not not_3 (not_3_out, B);
  or or_1 (F_A_prime_C_prime_B_prime, and_1_out, not_3_out);

  // Notes on the sheet:
  //   Logic Circut of #3 simplified Expression
  //   A'C'
  //   B'
endmodule

module Lab_5___4 (
  input  A,
  input  B,
  input  C,
  input  D,
  input  A_2,
  input  B_2,
  input  C_2,
  input  D_2,
  input  A_3,
  input  B_3,
  input  C_3,
  input  D_3,
  input  A_4,
  input  B_4,
  input  C_4,
  input  D_4,
  input  A_5,
  input  B_5,
  input  C_5,
  input  A_6,
  input  B_6,
  input  C_6,
  output out_23,
  output F_A_prime_B_AB_prime_CD_prime,
  output F_AB_prime_C_BD_prime_CD_prime,
  output F_A_prime_B_AC_D_prime,
  output F_C_prime,
  output F_BC_prime_B_prime_C
);

  wire and_1_out, and_2_out, and_3_out, and_4_out, and_5_out, and_6_out, and_7_out, and_8_out, and_9_out,
       and_10_out, and_11_out, and_12_out, and_13_out, not_1_out, not_2_out, not_3_out, not_4_out, not_5_out,
       not_6_out, not_7_out, not_8_out, not_9_out, not_11_out, not_12_out, not_13_out;

  not not_1 (not_1_out, B);
  not not_2 (not_2_out, C);
  not not_3 (not_3_out, D);
  not not_4 (not_4_out, A_2);
  not not_5 (not_5_out, B_2);
  not not_6 (not_6_out, D_2);
  not not_7 (not_7_out, B_3);
  not not_8 (not_8_out, A_4);
  not not_9 (not_9_out, D_4);
  not not_10 (F_C_prime, C_5);
  not not_11 (not_11_out, B_6);
  not not_12 (not_12_out, C_6);
  and and_1 (and_1_out, not_1_out, not_2_out);
  and and_2 (and_2_out, not_1_out, not_3_out);
  and and_3 (and_3_out, not_4_out, B_2);
  and and_4 (and_4_out, A_2, not_5_out);
  and and_5 (and_5_out, C_2, not_6_out);
  and and_6 (and_6_out, A_3, not_7_out, C_3);
  and and_7 (and_7_out, B_3, not_13_out);
  and and_8 (and_8_out, C_3, not_13_out);
  not not_13 (not_13_out, D_3);
  and and_9 (and_9_out, not_8_out, B_4);
  and and_10 (and_10_out, A_4, C_4);
  and and_11 (and_11_out, B_6, not_12_out);
  and and_12 (and_12_out, not_11_out, C_6);
  and and_13 (and_13_out, B, C, D);
  or or_1 (F_BC_prime_B_prime_C, and_11_out, and_12_out);
  or or_2 (out_23, and_1_out, and_2_out, and_13_out);
  or or_3 (F_A_prime_B_AB_prime_CD_prime, and_3_out, and_4_out, and_5_out);
  or or_4 (F_AB_prime_C_BD_prime_CD_prime, and_6_out, and_7_out, and_8_out);
  or or_5 (F_A_prime_B_AC_D_prime, and_9_out, and_10_out, not_9_out);

  // Notes on the sheet:
  //   #4 circuit 1 simplified:
  //   #4 circuit 2 simplified
  //   #4 circuit 3 simplified
  //   #4 circuit 4 simplified
  //   #4 circuit 5 simplified
  //   #4 circuit 6 simplified
  //   NOTE: After kmap, the A is cancelled out of the function
  //   B'C'
  //   AB'C
  //   A'B
  //   D'
  //   NOTE: kmap simplification cancelled A, B, A' and C' variables
  //   NOTE: kmap simplification canelled out the A variable
  //   BC'
  //   B'C
  //   B'D'
  //   BCD
  //   A'B
  //   AB'
  //   CD'
  //   BD'
  //   CD'
  //   AC
  //   F = B'C' + B'D'+BCD
endmodule
