// Logisim project Lab8.circ as structural Verilog: 4 circuits, main circuit 7seg
module Lab8_1 (
  input  A,
  input  B,
  input  C,
  input  D,
  input  A_2,
  input  B_2,
  input  C_2,
  input  D_2
);

  wire n7_seg_w_hex_1_a_2, n7_seg_w_hex_1_b_2, n7_seg_w_hex_1_c_2, n7_seg_w_hex_1_d_2, n7_seg_w_hex_1_e,
       n7_seg_w_hex_1_f, n7_seg_w_hex_1_g, n7seg_1_a_2, n7seg_1_b_2, n7seg_1_c_2, n7seg_1_d_2, n7seg_1_e,
       n7seg_1_f, n7seg_1_g;

  _7seg u_7seg_1 (
    .A(A), .B(B), .C(C), .D(D), .a_2(n7seg_1_a_2), .b_2(n7seg_1_b_2), .c_2(n7seg_1_c_2), .d_2(n7seg_1_d_2),
    .e(n7seg_1_e), .f(n7seg_1_f), .g(n7seg_1_g));
  _7_seg_w_hex u_7_seg_w_hex_1 (
    .A(A_2), .B(B_2), .C(C_2), .D(D_2), .a_2(n7_seg_w_hex_1_a_2), .b_2(n7_seg_w_hex_1_b_2),
    .c_2(n7_seg_w_hex_1_c_2), .d_2(n7_seg_w_hex_1_d_2), .e(n7_seg_w_hex_1_e), .f(n7_seg_w_hex_1_f),
    .g(n7_seg_w_hex_1_g));
  _7_Segment_Display u_7_segment_display_1 (
    .g(n7seg_1_g), .f(n7seg_1_f), .a(n7seg_1_a_2), .b(n7seg_1_b_2), .e(n7seg_1_e), .d(n7seg_1_d_2),
    .c(n7seg_1_c_2));  // open: dp
  _7_Segment_Display u_7_segment_display_2 (
    .g(n7_seg_w_hex_1_g), .f(n7_seg_w_hex_1_f), .a(n7_seg_w_hex_1_a_2), .b(n7_seg_w_hex_1_b_2),
    .e(n7_seg_w_hex_1_e), .d(n7_seg_w_hex_1_d_2), .c(n7_seg_w_hex_1_c_2));  // open: dp

  // Notes on the sheet:
  //   7 SEGMENT DISPLAY: 0-9 ONLY
  //   7 SEGMENT DISPLAY INCLUDING 0-9 AND A-F
endmodule

module _7seg (
  input  A,
  input  B,
  input  C,
  input  D,
  output a_2,
  output b_2,
  output c_2,
  output d_2,
  output e,
  output f,
  output g
);

  wire A_prime_B_out, A_prime_B_prime_C_out, A_prime_B_prime_out, A_prime_BC_prime_D_out,
       A_prime_BC_prime_out, A_prime_BD_out, A_prime_BD_prime_out, A_prime_C_out,
       A_prime_C_prime_D_prime_out, A_prime_CD_out, A_prime_CD_prime_out, A_prime_D_out,
       AB_prime_C_prime_out, B_prime_C_prime_D_prime_out, not_1_out, not_2_out, not_3_out, not_4_out;

  not not_1 (not_1_out, A);
  not not_2 (not_2_out, B);
  not not_3 (not_3_out, D);
  not not_4 (not_4_out, C);
  and A_prime_C (A_prime_C_out, not_1_out, C);
  and A_prime_BD (A_prime_BD_out, not_1_out, B, D);
  and B_prime_C_prime_D_prime (B_prime_C_prime_D_prime_out, not_2_out, not_4_out, not_3_out);
  and AB_prime_C_prime (AB_prime_C_prime_out, A, not_2_out, not_4_out);
  and A_prime_B_prime (A_prime_B_prime_out, not_1_out, not_2_out);
  and A_prime_C_prime_D_prime (A_prime_C_prime_D_prime_out, not_1_out, not_4_out, not_3_out);
  and A_prime_CD (A_prime_CD_out, not_1_out, C, D);
  and A_prime_B (A_prime_B_out, not_1_out, B);
  and A_prime_D (A_prime_D_out, not_1_out, D);
  and A_prime_CD_prime (A_prime_CD_prime_out, not_1_out, C, not_3_out);
  and A_prime_B_prime_C (A_prime_B_prime_C_out, not_1_out, not_2_out, C);
  and A_prime_BC_prime_D (A_prime_BC_prime_D_out, not_1_out, B, not_4_out, D);
  and A_prime_BC_prime (A_prime_BC_prime_out, not_1_out, B, not_4_out);
  and A_prime_BD_prime (A_prime_BD_prime_out, not_1_out, B, not_3_out);
  or or_1 (a_2, A_prime_C_out, A_prime_BD_out, B_prime_C_prime_D_prime_out, AB_prime_C_prime_out);
  or or_2 (b_2, A_prime_B_prime_out, A_prime_C_prime_D_prime_out, A_prime_CD_out, AB_prime_C_prime_out);
  or or_3 (c_2, A_prime_B_out, A_prime_D_out, B_prime_C_prime_D_prime_out, AB_prime_C_prime_out);
  or or_4 (d_2, A_prime_CD_prime_out, A_prime_B_prime_C_out, B_prime_C_prime_D_prime_out, AB_prime_C_prime_out, A_prime_BC_prime_D_out);
  or or_5 (e, A_prime_CD_prime_out, B_prime_C_prime_D_prime_out);
  or or_6 (f, A_prime_BC_prime_out, A_prime_C_prime_D_prime_out, A_prime_BD_prime_out, AB_prime_C_prime_out);
  or or_7 (g, A_prime_CD_prime_out, A_prime_B_prime_C_out, A_prime_BC_prime_out, AB_prime_C_prime_out);
endmodule

module _7_seg_w_hex (
  input  A,
  input  B,
  input  C,
  input  D,
  output a_2,
  output b_2,
  output c_2,
  output d_2,
  output e,
  output f,
  output g
);

  wire A_prime_B_out, A_prime_B_prime_D_prime_out, A_prime_B_prime_out, A_prime_BC_prime_out, A_prime_BD_out,
       A_prime_C_out, A_prime_C_prime_D_prime_out, A_prime_C_prime_out, A_prime_CD_out, A_prime_D_out,
       AB_out, AB_prime_C_prime_out, AB_prime_out, AC_out, AC_prime_D_out, AC_prime_D_prime_out, AD_out,
       AD_prime_out, B_prime_C_out, B_prime_CD_out, B_prime_D_prime_out, BC_out, BC_prime_D_out,
       BCD_prime_out, BD_prime_out, C_prime_D_out, C_prime_D_prime_out, CD_prime_out, not_1_out, not_2_out,
       not_3_out, not_4_out, or_1_out, or_2_out;

  not not_1 (not_1_out, A);
  not not_2 (not_2_out, B);
  not not_3 (not_3_out, C);
  not not_4 (not_4_out, D);
  and B_prime_D_prime (B_prime_D_prime_out, not_2_out, not_4_out);
  and A_prime_C (A_prime_C_out, not_1_out, C);
  and BC (BC_out, B, C);
  and AD_prime (AD_prime_out, A, not_4_out);
  and A_prime_BD (A_prime_BD_out, not_1_out, B, D);
  and AB_prime_C_prime (AB_prime_C_prime_out, A, not_2_out, not_3_out);
  and A_prime_B_prime (A_prime_B_prime_out, not_1_out, not_2_out);
  and A_prime_C_prime_D_prime (A_prime_C_prime_D_prime_out, not_1_out, not_3_out, not_4_out);
  and A_prime_CD (A_prime_CD_out, not_1_out, C, D);
  and AC_prime_D (AC_prime_D_out, A, not_3_out, D);
  and A_prime_C_prime (A_prime_C_prime_out, not_1_out, not_3_out);
  and A_prime_D (A_prime_D_out, not_1_out, D);
  and C_prime_D (C_prime_D_out, not_3_out, D);
  and A_prime_B (A_prime_B_out, not_1_out, B);
  and AB_prime (AB_prime_out, A, not_2_out);
  and A_prime_B_prime_D_prime (A_prime_B_prime_D_prime_out, not_1_out, not_2_out, not_4_out);
  and B_prime_CD (B_prime_CD_out, not_2_out, C, D);
  and BC_prime_D (BC_prime_D_out, B, not_3_out, D);
  and BCD_prime (BCD_prime_out, B, C, not_4_out);
  and AC_prime_D_prime (AC_prime_D_prime_out, A, not_3_out, not_4_out);
  and CD_prime (CD_prime_out, C, not_4_out);
  and AC (AC_out, A, C);
  and AB (AB_out, A, B);
  and C_prime_D_prime (C_prime_D_prime_out, not_3_out, not_4_out);
  and BD_prime (BD_prime_out, B, not_4_out);
  and A_prime_BC_prime (A_prime_BC_prime_out, not_1_out, B, not_3_out);
  and B_prime_C (B_prime_C_out, not_2_out, C);
  and AD (AD_out, A, D);
  or or_1 (or_1_out, B_prime_D_prime_out, A_prime_C_out, BC_out);
  or or_2 (or_2_out, AD_prime_out, A_prime_BD_out, AB_prime_C_prime_out);
  or or_3 (b_2, B_prime_D_prime_out, A_prime_B_prime_out, A_prime_C_prime_D_prime_out, A_prime_CD_out, AC_prime_D_out);
  or or_4 (c_2, A_prime_C_prime_out, A_prime_D_out, C_prime_D_out, A_prime_B_out, AB_prime_out);
  or or_5 (d_2, A_prime_B_prime_D_prime_out, B_prime_CD_out, BC_prime_D_out, BCD_prime_out, AC_prime_D_prime_out);
  or or_6 (e, B_prime_D_prime_out, CD_prime_out, AC_out, AB_out);
  or or_7 (f, AB_prime_out, AC_out, C_prime_D_prime_out, BD_prime_out, A_prime_BC_prime_out);
  or or_8 (g, CD_prime_out, AB_prime_out, B_prime_C_out, AD_out, A_prime_BC_prime_out);
  or or_9 (a_2, or_1_out, or_2_out);
endmodule

module Bin_to_Gray (
  input  B1,
  input  B2,
  input  B3,
  input  B4,
  output G1,
  output G2,
  output G3,
  output G4
);

  wire and_1_out, and_2_out, and_3_out, and_4_out, and_5_out, and_6_out, not_1_out, not_2_out, not_3_out,
       not_4_out;

  not not_1 (not_1_out, B1);
  not not_2 (not_2_out, B2);
  not not_3 (not_3_out, B3);
  not not_4 (not_4_out, B4);
  and and_1 (and_1_out, not_1_out, B2);
  and and_2 (and_2_out, B1, not_2_out);
  and and_3 (and_3_out, not_2_out, B3);
  and and_4 (and_4_out, B2, not_3_out);
  and and_5 (and_5_out, not_3_out, B4);
  and and_6 (and_6_out, B3, not_4_out);
  or or_1 (G2, and_1_out, and_2_out);
  or or_2 (G3, and_3_out, and_4_out);
  or or_3 (G4, and_5_out, and_6_out);

  assign G1 = B1;
endmodule
