// Logisim project Pearl_Jade Lab 2.circ as structural Verilog: 1 circuit, main circuit main
module main (
  input  in_1,
  input  in_2,
  input  _3_input_AND_Gate,
  input  in_4,
  input  in_5,
  input  in_6,
  input  in_7,
  input  _3_input_OR_Gate,
  input  in_9,
  input  in_10,
  input  in_11,
  input  in_12,
  input  _4_input_OR_Gate,
  input  in_14,
  input  in_15,
  input  in_16,
  input  in_17,
  input  in_18,
  input  in_19,
  input  in_20,
  input  in_21,
  input  in_22,
  input  in_23,
  input  in_24,
  output out_25,
  output out_26,
  output out_27,
  output out_28,
  output out_29,
  output out_30,
  output out_31
);

  wire and_1_out, and_2_out, and_3_out, and_5_out, or_1_out, or_2_out, or_3_out, or_4_out, or_5_out, or_7_out;

  and and_1 (and_1_out, in_11, in_11, in_12);
  and and_2 (and_2_out, in_15, in_17);
  and and_3 (and_3_out, _3_input_AND_Gate, in_6);
  and and_4 (out_27, and_3_out, in_7);
  and and_5 (and_5_out, and_1_out, and_2_out);
  and and_6 (out_30, and_5_out, in_19);
  and and_7 (out_26, in_2, in_5);
  or or_1 (or_1_out, in_20, in_21);
  or or_2 (or_2_out, in_22, in_23);
  or or_3 (or_3_out, _4_input_OR_Gate, in_14);
  or or_4 (or_4_out, in_16, in_18);
  or or_5 (or_5_out, or_1_out, or_2_out);
  or or_6 (out_25, in_1, in_4);
  or or_7 (or_7_out, _3_input_OR_Gate, in_9);
  or or_8 (out_29, or_3_out, or_4_out);
  or or_9 (out_31, or_5_out, in_24);
  or or_10 (out_28, or_7_out, in_10);

  // Notes on the sheet:
  //   5 input AND Gate
  //   2 input AND Gate
  //   5 input OR Gate
  //   2 input OR Gate
endmodule
