// Logisim project Pearl_Jade Lab 3.circ as structural Verilog: 5 circuits, main circuit NAND
module NAND (
  input  A,
  input  in_2,
  input  A_2,
  input  A_3,
  input  B,
  input  B_2,
  input  A_4,
  input  A_5,
  input  B_prime,
  input  B_3,
  output AA___A,
  output out_12,
  output out_13,
  output out_14,
  output out_15,
  output out_16
);

  wire nand_2_out, nand_3_out, nand_4_out;

  not not_1 (AA___A, A);
  and and_1 (out_13, A_2, B);
  or or_1 (out_15, A_4, B_prime);
  nand nand_1 (out_12, in_2, in_2);
  nand nand_2 (nand_2_out, A_3, B_2);
  nand nand_3 (nand_3_out, A_5, A_5);
  nand nand_4 (nand_4_out, B_3, B_3);
  nand nand_5 (out_14, nand_2_out, nand_2_out);
  nand nand_6 (out_16, nand_3_out, nand_4_out);

  // Notes on the sheet:
  //   (A+B)' = A'B'
  //   (AB)' = A' + B'
  //   A'' = A
  //   DE MORGAN'S THEOREM
  //   Exercise 1: NOT GATE USING ONLY 2 INPUT NAND GATE
  //   Exercise 2: BUILD AND GATE USING ONLY 2 INPUTS NAND GATE
  //   Exercise 3: OR GATE USING ONLY 2 INPUT NAND GATE
  //   ANY BOOLEAN FUNCTION CAN BE IMPLEMENTED USING ONLY NAND GATES
  //   (AA)' = A'
  //   (AB)'
  //   A'
  //   B'
  //   (AB)' '= AB
  //   (A'B')' = A'' + B'' = A+B
endmodule

module NOR (
  input  in_1,
  input  in_2,
  input  in_3,
  input  in_4,
  input  DE_MORGAN_S_THM,
  input  in_6,
  input  in_7,
  input  in_8,
  input  in_9,
  input  in_10,
  output out_11,
  output A_A___A,
  output out_13,
  output out_14,
  output out_15,
  output out_16
);

  wire nor_2_out, nor_3_out, nor_4_out;

  not not_1 (out_11, in_1);
  and and_1 (out_13, in_4, DE_MORGAN_S_THM);
  or or_1 (out_15, in_8, in_9);
  nor nor_1 (A_A___A, in_2, in_2);
  not nor_2 (nor_2_out, in_3);  // NOR_Gate
  not nor_3 (nor_3_out, in_6);  // NOR_Gate
  nor nor_4 (nor_4_out, in_7, in_10);
  nor nor_5 (out_14, nor_2_out, nor_3_out);
  not nor_6 (out_16, nor_4_out);  // NOR_Gate

  // Notes on the sheet:
  //   (A+B)' = A'B'
  //   Exercise 1: BUILD NOT GATE USING ONLY 2 INPUT NOR GATE
  //   Exercise 2: BUILD AND GATE USING ONLY 2 INPUT NOR GATE
  //   Exercise 3: BUILD OR GATE USING ONLY NOR GATE
  //   ANY BOOLEAN FUNCTION CAN BE IMPLEMENTED USING ONLY NOR GATES
  //   (A+A)' = A'
endmodule

module LOGIC_CIRCUIT_ANALYSIS (
  input  A,
  input  B,
  output out_3
);

  wire nand_1_out, not_1_out, or_1_out;

  not not_1 (not_1_out, A);
  nand nand_1 (nand_1_out, not_1_out, B);
  or or_1 (or_1_out, A, B);
  and and_1 (out_3, nand_1_out, or_1_out);

  // Notes on the sheet:
  //   F
  //   A   B
  //   0  0
  //   0  1
  //   1  0
  //   1  1
  //   A'
  //   A'B
  //   1
  //   1
  //   0
  //   0
  //   1
  //   0
  //   1
  //   0
  //   1
  //   0
  //   0
  //   1
  //   1
  //   1
  //   0
  //   0
  //   A'
  //   (A'B)'
  //   A+B
  //   0
  //   1
  //   1
  //   1
  //   F = (A'B)' (A+B)
  //   0
  //   0
  //   1
  //   1
  //   DERIVE THE BOOLEAN FUNCTION / EXPRESSION / EQUATION
  //   DRAW THE TRUTH TABLE OF THE CIRCUIT
  //   (A' B)'
  //   A+B
  //   N = 1
  //   N = 2
  //   N = 3
  //   N = 4
  //   N
  //   F = (A'B)' ( A+B)
  //   N = NUMBER OF INPUTS
  //   2
  //   4
  //   8
  //   16
  //   2^N
  //   POSSIBLE OUTPUTS
endmodule

module LAB_3_Exercises (
  input  A,
  input  A_2,
  input  B,
  input  B_2,
  output F___A_prime_B__prime__A_prime_B,
  output out_6
);

  wire and_2_out, nand_1_out, nor_1_out, not_1_out, not_2_out, not_3_out, or_1_out;

  not not_1 (not_1_out, A);
  not not_2 (not_2_out, A);
  or or_1 (or_1_out, not_2_out, B);
  nor nor_1 (nor_1_out, not_1_out, B);
  and and_1 (F___A_prime_B__prime__A_prime_B, nor_1_out, or_1_out);
  not not_3 (not_3_out, A_2);
  nand nand_1 (nand_1_out, A_2, B_2);
  and and_2 (and_2_out, not_3_out, B_2);
  or or_2 (out_6, nand_1_out, and_2_out);

  // Notes on the sheet:
  //   A'
  //   B
  //   A'
  //   B
  //   DERIVE BOOLEAN EXPRESSIONS AND DRAW THE TRUTH TABLES
  //   (A' B)'
  //   A' + B
  //   A
  //   B
  //   A'
  //   B
  //   (A'B)
  //   (A B)'
  //   F = (A B)' + (A' B)
endmodule

module LAB_3_TRUTH_TABLE (
  input  in_1,
  input  in_2,
  input  in_3,
  output out_4
);

  wire and_1_out, and_2_out, and_3_out, not_1_out;

  not not_1 (not_1_out, in_1);
  and and_1 (and_1_out, in_1, in_2);
  and and_2 (and_2_out, not_1_out, in_2);
  and and_3 (and_3_out, in_1, in_2, in_3);
  or or_1 (out_4, and_1_out, and_2_out, and_3_out);

  // Notes on the sheet:
  //   000
  //   011
  //   101
  //   110
  //   F = AB + A'B + ABC
  //   AB
  //   ABC
  //   0
  //   0
  //   001
  //   0
  //   010
  //   0
  //   0
  //   100
  //   0
  //   0
  //   1
  //   111
  //   A'B
  //   A'
  //   1
  //   0
  //   1
  //   0
  //   1
  //   1
  //   1
  //   1
  //   0
  //   0
  //   0
  //   0
  //   0
  //   0
  //   0
  //   0
  //   ABC
  //   0
  //   0
  //   0
  //   0
  //   0
  //   0
  //   0
  //   1
  //   DERIVE THE TRUTH TABLE
  //   F
  //   0
  //   0
  //   1
  //   1
  //   0
  //   0
  //   1
  //   1
endmodule
