// Logisim project HEX 7seg.circ as structural Verilog: 1 circuit, main circuit main
module main (
  input  in_1,
  input  in_2,
  input  in_3,
  input  in_4
);

  wire A_out, and_1_out, and_2_out, and_3_out, and_4_out, and_5_out, and_6_out, and_7_out, and_8_out,
       and_9_out, and_10_out, and_11_out, and_12_out, and_13_out, and_14_out, and_15_out, and_16_out,
       and_17_out, and_18_out, and_19_out, and_20_out, and_21_out, and_22_out, and_23_out, and_24_out,
       and_25_out, and_26_out, and_27_out, and_28_out, and_29_out, and_30_out, and_31_out, and_32_out,
       and_33_out, and_34_out, and_35_out, B_out, C_out, D_out, E_out, F_out, G_out, not_1_out, not_2_out,
       not_3_out, not_4_out;

  not not_1 (not_1_out, in_4);
  not not_2 (not_2_out, in_3);
  not not_3 (not_3_out, in_2);
  not not_4 (not_4_out, in_1);
  and and_1 (and_1_out, not_2_out, not_4_out);
  and and_2 (and_2_out, not_1_out, not_2_out);
  and and_3 (and_3_out, not_1_out, not_3_out);
  and and_4 (and_4_out, in_4, not_3_out);
  and and_5 (and_5_out, not_2_out, not_4_out);
  and and_6 (and_6_out, not_3_out, not_4_out, not_4_out);
  and and_7 (and_7_out, not_2_out, in_2);
  and and_8 (and_8_out, not_1_out, in_2);
  and and_9 (and_9_out, in_3, in_2);
  and and_10 (and_10_out, not_2_out, not_4_out);
  and and_11 (and_11_out, not_1_out, not_3_out, not_4_out);
  and and_12 (and_12_out, not_1_out, in_1);
  and and_13 (and_13_out, not_3_out, in_1);
  and and_14 (and_14_out, not_1_out, not_2_out, not_4_out);
  and and_15 (and_15_out, not_2_out, in_2, in_1);
  and and_16 (and_16_out, in_2, not_4_out);
  and and_17 (and_17_out, in_4, in_2);
  and and_18 (and_18_out, in_3, not_4_out);
  and and_19 (and_19_out, in_4, not_2_out);
  and and_20 (and_20_out, in_2, not_4_out);
  and and_21 (and_21_out, in_4, not_2_out);
  and and_22 (and_22_out, in_4, not_4_out);
  and and_23 (and_23_out, not_1_out, in_2, in_1);
  and and_24 (and_24_out, not_1_out, in_3);
  and and_25 (and_25_out, in_3, not_3_out, in_1);
  and and_26 (and_26_out, in_4, in_3);
  and and_27 (and_27_out, in_4, in_2);
  and and_28 (and_28_out, in_4, in_1);
  and and_29 (and_29_out, not_1_out, in_3, in_1);
  and and_30 (and_30_out, in_4, not_2_out, not_3_out);
  and and_31 (and_31_out, in_4, not_3_out, in_1);
  and and_32 (and_32_out, in_4, not_2_out);
  and and_33 (and_33_out, in_3, in_2, not_4_out);
  and and_34 (and_34_out, not_1_out, in_3, not_3_out);
  and and_35 (and_35_out, not_1_out, in_3, not_3_out);
  or A (A_out, and_1_out, and_8_out, and_9_out, and_22_out, and_29_out, and_30_out);
  or B (B_out, and_2_out, and_10_out, and_11_out, and_23_out, and_31_out);
  or C (C_out, and_3_out, and_12_out, and_13_out, and_24_out, and_32_out);
  or D (D_out, and_4_out, and_14_out, and_15_out, and_25_out, and_33_out);
  or E (E_out, and_5_out, and_16_out, and_17_out, and_26_out);
  or F (F_out, and_6_out, and_18_out, and_19_out, and_27_out, and_34_out);
  or G (G_out, and_7_out, and_20_out, and_21_out, and_28_out, and_35_out);
  _7_Segment_Display u_7_segment_display_1 (
    .g(G_out), .f(F_out), .a(A_out), .b(B_out), .e(E_out), .d(D_out), .c(C_out));  // open: dp
endmodule
