// Logisim project XOR Gate.circ as structural Verilog: 1 circuit, main circuit main
module main (
  input  in_1,
  input  in_2,
  input  in_3,
  input  in_4,
  output out_5,
  output out_6
);

  wire and_1_out, and_2_out, not_1_out, not_2_out;

  xor xor_1 (out_5, in_1, in_2);
  not not_1 (not_1_out, in_3);
  not not_2 (not_2_out, in_4);
  and and_1 (and_1_out, not_1_out, in_4);
  and and_2 (and_2_out, in_3, not_2_out);
  or or_1 (out_6, and_1_out, and_2_out);

  // Notes on the sheet:
  //   A'B + AB'
endmodule
